# Fritzing sketch Amplifier (saved by Fritzing 0.9.3b)
circuit board: 7.46788cm x 4.07474cm
breadboards: 1

parts:
  Juan_Rodriguez = Adafruit MAX98357A I2S 3W Class D Amplifier [part_number="Adafruit #3006"]
  Raspberry_Pi_1 = Raspberry Pi 3 [part_number=RPI-3-V1.2]

nets:
  VIN: Juan_Rodriguez.VIN, Raspberry_Pi_1.5V
  GND: Juan_Rodriguez.GND, Raspberry_Pi_1.GND
  N1: Juan_Rodriguez.DIN, Raspberry_Pi_1.GPIO21
  N2: Juan_Rodriguez.BCLK, Raspberry_Pi_1.GPIO18
  N3: Juan_Rodriguez.LRCLK, Raspberry_Pi_1.GPIO19

custom parts:
  Adafruit MAX98357A I2S 3W Class D Amplifier: Listen to this good news - we now have an all in one digital audio amp breakout board that works incredibly well with the Raspberry Pi! If you're looking for an easy and low cost way to get you digital sound files bumpin' then the MAX08357 I2S Amp Breakout is for you. It takes standard I2S digital audio input and, not only decodes it into analog, but also amplifies it directly into a speaker.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
