# Fritzing sketch 3Sensors (saved by Fritzing 0.9.3b)
circuit board: 8.52596cm x 6.42695cm
breadboards: 1

parts:
  Juan_Rodriguez = Seven-Segment LED Backpack 1.2 Inch Digits [part_number=1268]
  Amplifier = Adafruit MAX98357A I2S 3W Class D Amplifier [part_number="Adafruit #3006"]
  Temperature = HTU21D-F Temperature + Humidity Sensor
  Raspberry_Pi_1 = Raspberry Pi 3 [part_number=RPI-3-V1.2]

nets:
  N1: Juan_Rodriguez.SCL, Temperature.SCL, Raspberry_Pi_1.GPIO3
  N2: Juan_Rodriguez.SDA, Temperature.SDA, Raspberry_Pi_1.GPIO2
  GND: Juan_Rodriguez.GND, Amplifier.GND, Temperature.GND, Raspberry_Pi_1.GND
  VIN: Juan_Rodriguez.VDD, Amplifier.VIN, Temperature.VIN, Raspberry_Pi_1.5V
  3V3: Juan_Rodriguez.VCCIO, Temperature.+3V3, Raspberry_Pi_1.3v3, Raspberry_Pi_1.3V3
  N3: Amplifier.DIN, Raspberry_Pi_1.GIPO21
  N4: Amplifier.BCLK, Raspberry_Pi_1.GIPO18
  N5: Amplifier.LRCLK, Raspberry_Pi_1.GIPO19

custom parts:
  Seven-Segment LED Backpack 1.2 Inch Digits: This jumbo 1.2" 7-segment LED display includes a driver chip for simple control via an I2C interface. The backpack features address-selection jumpers so you can connect up to eight displays on a single I2C bus.
  Adafruit MAX98357A I2S 3W Class D Amplifier: Listen to this good news - we now have an all in one digital audio amp breakout board that works incredibly well with the Raspberry Pi! If you're looking for an easy and low cost way to get you digital sound files bumpin' then the MAX08357 I2S Amp Breakout is for you. It takes standard I2S digital audio input and, not only decodes it into analog, but also amplifies it directly into a speaker.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
  HTU21D-F Temperature + Humidity Sensor: This I2C digital humidity sensor is an accurate and intelligent alternative to the much simpler Humidity and Temperature Sensor - SHT15 Breakout It has a typical accuracy of ±2% with an operating range that's optimized from 5% to 95% RH. Operation outside this range is still possible - just the accuracy might drop a bit. The temperature output has an accuracy of ±1°C from -30~90°C. If you're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
