# Fritzing sketch 4DigitDisplay (saved by Fritzing 0.9.3b)
circuit board: 9.41388cm x 6.07399cm
breadboards: 1

parts:
  Juan_Rodriguez = Seven-Segment LED Backpack 1.2 Inch Digits [part_number=1268]
  Raspberry_Pi_1 = Raspberry Pi 3 [part_number=RPI-3-V1.2]

nets:
  N1: Juan_Rodriguez.SCL, Raspberry_Pi_1.GPIO3
  N2: Juan_Rodriguez.SDA, Raspberry_Pi_1.GPIO2
  GND: Juan_Rodriguez.GND, Raspberry_Pi_1.GND
  VDD: Juan_Rodriguez.VDD, Raspberry_Pi_1.5V
  3V3: Juan_Rodriguez.VCCIO, Raspberry_Pi_1.3v3, Raspberry_Pi_1.3V3

custom parts:
  Seven-Segment LED Backpack 1.2 Inch Digits: This jumbo 1.2" 7-segment LED display includes a driver chip for simple control via an I2C interface. The backpack features address-selection jumpers so you can connect up to eight displays on a single I2C bus.
